// Logisim project exp6-1a.circ as structural Verilog: 1 circuit, main circuit main
module main (
  input  A,
  input  B,
  input  C,
  output out_4
);

  wire and_1_out, not_1_out, not_2_out, not_3_out;

  not not_1 (not_1_out, A);
  not not_2 (not_2_out, B);
  and and_1 (and_1_out, not_1_out, not_2_out);
  not not_3 (not_3_out, C);
  or or_1 (out_4, and_1_out, not_3_out);

  // Notes on the sheet:
  //   Sarah Strickman
  //   CSCI.250.02
  //   Experiment 6
  //   Activity 1a
  //   Due: Nov 8. 2019
endmodule
