// Logisim project exp6-1b.circ as structural Verilog: 1 circuit, main circuit main
module main (
  input  [2:0] A_B_C,
  output out_2
);

  wire decoder_1_out0, decoder_1_out1, decoder_1_out2, decoder_1_out4, decoder_1_out6;

  Decoder #(.select(3), .tristate("false")) decoder_1 (
    .out0(decoder_1_out0), .out1(decoder_1_out1), .out2(decoder_1_out2), .out4(decoder_1_out4),
    .out6(decoder_1_out6), .sel(A_B_C));  // open: out3, out5, out7
  or or_1 (out_2, decoder_1_out0, decoder_1_out1, decoder_1_out2, decoder_1_out4, decoder_1_out6);

  // Notes on the sheet:
  //   Sarah Strickman
  //   CSCI.250.02
  //   Experiment 6
  //   Activite 1c
  //   Due: Nov 9. 2019
endmodule
